# Fritzing sketch weather display (saved by Fritzing 1.0.6)

parts:
  Part1 = LCD1602-I2C
  U1 = LuaNode32 / ESP32 [part_number=ESP32S-PIN30]

nets:
  GND: Part1.GND, U1.GND
  VCC: Part1.VCC, U1.Vin
  N1: Part1.SDA, U1.D21
  N2: Part1.SCL, U1.D22

custom parts:
  LCD1602-I2C: A standard character display, usually with 2x16 characters. Comes in many colors with LCM1602 IIC attached.
  LuaNode32 / ESP32: New Image for LuaNode32 DOIT ESP32 DEVKIT V1. Base parts from LuaNode32 / ESP32 ESP32 based LuaNode32 by G.Noorlander DOIT Esp32 DevKit v1 (30 pins long, 11 pins width) by Werner Rothschopf (modified by vanepp Dec 2018)
